# Fritzing sketch weather (saved by Fritzing 0.9.4)
circuit board: 6cm x 4cm
breadboards: 1

parts:
  ESP-12F = Gizwits WiFi Witty ESP-12F
  DHT11 = Humidity and Temperature Sensor RHT03
  C2 = Ceramic Capacitor [capacitance="100 nF" package="1206 [SMD, multilayer]"]
  U1 = Voltage Regulator - 3.3V [package="TO220 [THT]"]
  S1_RESET = Pushbutton [package="[THT]"]
  S2_MODE = Pushbutton [package="[THT]"]
  R1 = Resistor [tolerance=±5% resistance=10k package=THT]
  R2 = Resistor [tolerance=±5% resistance=10k package=THT]
  R3 = Resistor [tolerance=±5% resistance=220k package=THT]
  R4 = Resistor [tolerance=±5% resistance=68k package=THT]
  Li-ion_4_2V = Battery
  C1 = Electrolytic Capacitor [capacitance=1000µF package="300 mil [THT, electrolytic]"]

nets:
  N1: ESP-12F.REST, ESP-12F.GPIO16, S1_RESET.Pin_3, S1_RESET.Pin_4, R2.Pin_1
  N2: ESP-12F.ADC, R3.Pin_1, R4.Pin_0
  VCC: ESP-12F.CH_PD, ESP-12F.VCC, DHT11.Vcc, C2.1, U1.output_voltage, S2_MODE.Pin_3, S2_MODE.Pin_4, R2.Pin_0, C1.+
  N3: ESP-12F.GPIO14, S2_MODE.Pin_1, S2_MODE.Pin_2, R1.Pin_0
  GND: ESP-12F.GND, DHT11.GND_2, C2.0, U1.GND, S1_RESET.Pin_1, S1_RESET.Pin_2, R1.Pin_1, R4.Pin_1, Li-ion_4_2V.-, C1.-
  N4: ESP-12F.GPIO4, DHT11.Data-signal
  N5: U1.input_voltage, R3.Pin_0, Li-ion_4_2V.+
